// Logisim project Practica5.circ as structural Verilog
module Flip_Flop_SR (
  input  S,
  input  R,
  output Q,
  output Q_prime
);

  wire clock_1_out;

  Clock clock_1 (.out(clock_1_out));
  nor nor_1 (Q, S, clock_1_out, Q_prime);
  nor nor_2 (Q_prime, Q, clock_1_out, R);
endmodule
